# Fritzing sketch emg_circuit (saved by Fritzing 0.8.7b)
circuit board: 10cm x 6cm
breadboards: 1

parts:
  R1 = Resistor [tolerance=±10% resistance=100 package=THT]
  AD620ANZ1 = AD620ANZ DIP [chip_label=AD620 package="DIP (Dual Inline) [THT]"]
  3_5mm_jack1 = 3.5mm jack for EMG electrode [part_number="LUMBERG JEITA RC-5325A" package="RC-5325A [SMD]"]
  U1 = LIPO-1000mAh [package=lipo-1000]
  ADM660ANZ1 = ADM660ANZ DIP [chip_label=ADM660 package="DIP (Dual Inline) [THT]"]
  C3 = Electrolytic Capacitor [capacitance=1000μF package="1010 [SMD, electrolytic]"]
  C4 = Electrolytic Capacitor [capacitance=1000μF package="1010 [SMD, electrolytic]"]
  TL1 = TL084CN [package=dil14]
  C5 = Electrolytic Capacitor [capacitance=1000μF package="1010 [SMD, electrolytic]"]
  R2 = Resistor [tolerance=±10% resistance=10k package=THT]
  D1 = Diode [package=diode-1n4001]
  D2 = Diode [package=diode-1n4001]
  R3 = Resistor [tolerance=±10% resistance=10k package=THT]
  R4 = Resistor [tolerance=±10% resistance=20k package=THT]
  R5 = Resistor [tolerance=±10% resistance=20k package=THT]
  R6 = Resistor [tolerance=±10% resistance=1k package=THT]
  R7 = Rotary Potentiometer (Small) [maximum_resistance=10kΩ package=THT]

nets:
  N1: R1.Pin_0, AD620ANZ1.pin8
  N2: R1.Pin_1, AD620ANZ1.pin1
  N3: AD620ANZ1.pin2, 3_5mm_jack1.RING2
  N4: AD620ANZ1.pin3, 3_5mm_jack1.RING1
  N5: AD620ANZ1.pin4, ADM660ANZ1.pin5, C4.-, TL1.11
  N6: AD620ANZ1.pin5, 3_5mm_jack1.SLEEVE, U1.-, ADM660ANZ1.pin3, ADM660ANZ1.pin6, C4.+, TL1.5, TL1.10
  N7: AD620ANZ1.pin6, C5.-
  N8: AD620ANZ1.pin7, U1.+, ADM660ANZ1.pin8, TL1.4
  N9: ADM660ANZ1.pin2, C3.-
  N10: ADM660ANZ1.pin4, C3.+
  N11: TL1.1, R7.wiper
  N12: TL1.2, R6.Pin_1, R7.leg1
  N13: TL1.3, TL1.8, R4.Pin_0
  N14: TL1.6, R2.Pin_1
  N15: TL1.7, D1.A
  N16: TL1.9, R3.Pin_1, R4.Pin_1, R5.Pin_1
  N17: C5.+, R2.Pin_0, R5.Pin_0
  N18: D2.A, R3.Pin_0

notes:
  EMG circuit for bruxism monitor
  color conventions:
  green: +V (supply)
  black: GND
  orange: -V (supply)
  blue: electrode blue cable
  red: electrode red cable
  brown: stage 1 wires
  purple: stage 2 wires
  yellow: stage 3 wires
  grey: signal wire

custom parts:
  AD620ANZ DIP: A DIP stand-in part for whatever IC you want. With 8 pins on a 300mil dual inline package (DIP) footprint.
  3.5mm jack for EMG electrode: Smartphone audio jack with 4 pins (stereo plus microphone), based on the LUMBERG JEITA RC-5325A
  ADM660ANZ DIP: A DIP stand-in part for whatever IC you want. With 8 pins on a 300mil dual inline package (DIP) footprint.
  TL084CN: TL084CN http://hk.mouser.com/Search/ProductDetail.aspx?R=TL084CNvirtualkey59500000virtualkey595-TL084CN
